# Fritzing sketch Prototype (saved by Fritzing 0.9.3b)
breadboards: 1

parts:
  Arduino_Board = Arduino Uno (Rev3)
  J1 = Basic Servo
  Motor_1 = DC Motor
  Motor_2 = DC Motor
  Ultra_sonic_sensor = hc-sr04
  Color_Sensor = HDJD-S822-QR999 [package=qfn-16]
  Motor_Driver = Dual VNH2SP30 Motor Driver [part_number=MD03A]
  LiPo_Battery = Battery Holders [package=lipo-1100mAh]
  Power_Distribution_board = Arduino Power Driver Shield

nets:
  N1: Arduino_Board.A4/SDA, Color_Sensor.GSBLUE1
  N2: Arduino_Board.A5/SCL, Color_Sensor.GSRED0
  N3: Arduino_Board.D9_PWM, J1.pulse
  N4: Arduino_Board.D11_PWM/MOSI, Motor_Driver.1DIAG/EN
  N5: Arduino_Board.D12/MISO, Ultra_sonic_sensor.Echo
  N6: Arduino_Board.D13/SCK, Ultra_sonic_sensor.Trig
  N7: Arduino_Board.D3_PWM, Motor_Driver.2DIAG/EN
  N8: Arduino_Board.D4, Motor_Driver.2INb#143
  N9: Arduino_Board.D5_PWM, Motor_Driver.2INb#142
  N10: Arduino_Board.D7, Motor_Driver.1INa
  VCC: Arduino_Board.5V, J1.vcc, Ultra_sonic_sensor.VCC, Color_Sensor.VDD3
  GND: Arduino_Board.GND, J1.gnd, Ultra_sonic_sensor.GND, Color_Sensor.GND
  N11: Motor_1.pin_1, Motor_Driver.OUT_2A
  N12: Motor_1.pin_2, Motor_Driver.OUT_2B
  N13: Motor_2.pin_1, Motor_Driver.OUT_1A
  N14: Motor_2.pin_2, Motor_Driver.OUT_1B
  VIN: Motor_Driver.VIN, Power_Distribution_board.12V
  N15: Motor_Driver.GND, Power_Distribution_board.D6-12V
  N16: LiPo_Battery.+, Power_Distribution_board.VIN
  N17: LiPo_Battery.-, Power_Distribution_board.GND
