# Fritzing sketch motorTestDiagram (saved by Fritzing 0.9.3b)
breadboards: 1

parts:
  Part1 = Arduino Uno (Rev3)
  Q1 = Basic FET N-Channel [package="TO220 [THT]"]
  M1 = DC Motor

nets:
  N1: Part1.D9_PWM, Q1.drain, M1.pin_2
  N2: Part1.5V, Q1.source
  N3: Part1.GND, M1.pin_1
